// Logisim project 13.circ as structural Verilog: 1 circuit, main circuit main
module main (
  input  in_1,
  input  in_2,
  output [7:0] out_3
);

  wire and_1_out, and_2_out, comparator_2_eq, comparator_2_gt, decoder_1_out0, decoder_1_out1,
       decoder_1_out2, decoder_1_out3, nor_1_out, not_1_out, not_2_out, undriven, xor_1_out, xor_2_out;
  wire [7:0] adder_1_out, adder_2_out, CAR_q, controlled_buffer_1_out, counter_1_q, OutsideMemory_data;

  Register CAR (.D(adder_2_out), .en(undriven), .Q(CAR_q), .clk(in_2), .clr(in_1));
  Adder adder_1 (.a(controlled_buffer_1_out), .b(CAR_q), .out(adder_1_out));  // open: cin, cout
  Adder adder_2 (.a(8'h1), .b(CAR_q), .out(adder_2_out));  // open: cin, cout
  Counter #(.max('h2)) counter_1 (
    .count(comparator_2_gt), .Q(counter_1_q), .clk(in_2), .clr(not_1_out));  // open: load, D, carry, up
  not not_1 (not_1_out, comparator_2_gt);
  Register NAR (.D(adder_1_out), .en(comparator_2_eq), .Q(out_3), .clk(in_2));  // open: clr
  Comparator comparator_1 (.a(controlled_buffer_1_out), .b(counter_1_q));  // open: gt, eq, lt
  Comparator comparator_2 (.a(out_3), .b(CAR_q), .gt(comparator_2_gt), .eq(comparator_2_eq));  // open: lt
  ROM OutsideMemory (.addr(CAR_q), .data(OutsideMemory_data));
  Decoder #(.select(2)) decoder_1 (
    .out0(decoder_1_out0), .out1(decoder_1_out1), .out2(decoder_1_out2), .out3(decoder_1_out3),
    .sel(counter_1_q[1:0]), .en(comparator_2_gt));
  assign controlled_buffer_1_out = nor_1_out ? 8'h1 : 8'bz;  // Controlled_Buffer controlled_buffer_1
  nor nor_1 (nor_1_out, OutsideMemory_data[1], OutsideMemory_data[0]);
  assign controlled_buffer_1_out = xor_1_out ? 8'h2 : 8'bz;  // Controlled_Buffer controlled_buffer_2
  xor xor_1 (xor_1_out, OutsideMemory_data[1], and_1_out);
  assign controlled_buffer_1_out = xor_2_out ? 8'h3 : 8'bz;  // Controlled_Buffer controlled_buffer_3
  xor xor_2 (xor_2_out, and_1_out, OutsideMemory_data[0]);
  assign controlled_buffer_1_out = and_2_out ? 8'h4 : 8'bz;  // Controlled_Buffer controlled_buffer_4
  not not_2 (not_2_out, comparator_2_gt);
  and and_1 (and_1_out, OutsideMemory_data[0], OutsideMemory_data[1]);
  and and_2 (and_2_out, OutsideMemory_data[0], OutsideMemory_data[1]);
  Register register_1 (.D(OutsideMemory_data), .en(not_2_out), .clk(in_2));  // open: Q, clr
  Register register_2 (.D(OutsideMemory_data), .en(decoder_1_out0), .clk(in_2));  // open: Q, clr
  Register register_3 (.D(OutsideMemory_data), .en(decoder_1_out1), .clk(in_2));  // open: Q, clr
  Register register_4 (.D(OutsideMemory_data), .en(decoder_1_out2), .clk(in_2));  // open: Q, clr
  Register register_5 (.D(OutsideMemory_data), .en(decoder_1_out3));  // open: Q, clk, clr

  // Other names for the same wires on the sheet: CLK = in_2

  // Notes on the sheet:
  //   contents of OutsideMemory (hex, n*v repeats v):
  //   0 0 1 4 3 6
endmodule
