// Logisim project 14.circ as structural Verilog: 1 circuit, main circuit main
module main (
  input  in_1,
  input  in_2,
  input  [7:0] in_3,
  input  in_4,
  input  in_5,
  input  in_6,
  input  in_7,
  input  in_8,
  input  in_9,
  input  in_10,
  input  in_11,
  input  [7:0] in_12,
  output [7:0] out_13
);

  wire adder_3_cout, and_1_out, and_2_out, CLK, comparator_2_eq, comparator_2_gt, comparator_4_gt,
       comparator_5_gt, comparator_6_gt, decoder_1_out0, decoder_1_out1, decoder_1_out2, decoder_1_out3,
       nor_1_out, not_1_out, not_2_out, not_3_out, subtractor_1_bout, undriven, undriven_2, undriven_3,
       undriven_4, undriven_5, undriven_6, undriven_7, xor_1_out, xor_2_out, xor_3_out, xor_5_out;
  wire [2:0] comparator_3_gt;
  wire [7:0] adder_1_out, adder_2_out, adder_3_out, CAR_q, controlled_buffer_1_out, controlled_buffer_5_out,
       controlled_buffer_11_out, controlled_buffer_13_out, counter_1_q, divider_1_out, divider_1_rem,
       multiplier_1_cout, multiplier_1_out, multiplier_2_cout, multiplier_2_out, multiplier_3_out,
       multiplier_4_out, OutsideMemory_data, register_6_q, register_7_q, register_9_q, register_10_q,
       register_11_q, register_12_q, subtractor_1_out;

  Register CAR (.D(adder_2_out), .en(undriven), .Q(CAR_q), .clk(CLK), .clr(in_1));
  Adder adder_1 (.a(controlled_buffer_1_out), .b(CAR_q), .out(adder_1_out));  // open: cin, cout
  Adder adder_2 (.a(8'h1), .b(CAR_q), .out(adder_2_out));  // open: cin, cout
  Counter #(.max('h2)) counter_1 (
    .count(comparator_2_gt), .Q(counter_1_q), .clk(CLK), .clr(not_1_out));  // open: load, D, carry, up
  not not_1 (not_1_out, comparator_2_gt);
  Register NAR (.D(adder_1_out), .en(comparator_2_eq), .Q(out_13), .clk(CLK));  // open: clr
  Comparator comparator_1 (.a(controlled_buffer_1_out), .b(counter_1_q));  // open: gt, eq, lt
  Comparator comparator_2 (.a(out_13), .b(CAR_q), .gt(comparator_2_gt), .eq(comparator_2_eq));  // open: lt
  ROM OutsideMemory (.addr(CAR_q), .data(OutsideMemory_data));
  Decoder #(.select(2)) decoder_1 (
    .out0(decoder_1_out0), .out1(decoder_1_out1), .out2(decoder_1_out2), .out3(decoder_1_out3),
    .sel(counter_1_q[1:0]), .en(comparator_2_gt));
  assign controlled_buffer_1_out = nor_1_out ? 8'h1 : 8'bz;  // Controlled_Buffer controlled_buffer_1
  nor nor_1 (nor_1_out, OutsideMemory_data[1], OutsideMemory_data[0]);
  assign controlled_buffer_1_out = xor_1_out ? 8'h2 : 8'bz;  // Controlled_Buffer controlled_buffer_2
  xor xor_1 (xor_1_out, OutsideMemory_data[1], and_1_out);
  assign controlled_buffer_1_out = xor_2_out ? 8'h3 : 8'bz;  // Controlled_Buffer controlled_buffer_3
  xor xor_2 (xor_2_out, and_1_out, OutsideMemory_data[0]);
  assign controlled_buffer_1_out = and_2_out ? 8'h4 : 8'bz;  // Controlled_Buffer controlled_buffer_4
  not not_2 (not_2_out, comparator_2_gt);
  and and_1 (and_1_out, OutsideMemory_data[0], OutsideMemory_data[1]);
  and and_2 (and_2_out, OutsideMemory_data[0], OutsideMemory_data[1]);
  Register register_1 (.D(OutsideMemory_data), .en(not_2_out), .clk(CLK));  // open: Q, clr
  Register register_2 (.D(OutsideMemory_data), .en(decoder_1_out0), .clk(CLK));  // open: Q, clr
  Register register_3 (.D(OutsideMemory_data), .en(decoder_1_out1), .clk(CLK));  // open: Q, clr
  Register register_4 (.D(OutsideMemory_data), .en(decoder_1_out2), .clk(CLK));  // open: Q, clr
  Register register_5 (.D(OutsideMemory_data), .en(decoder_1_out3));  // open: Q, clk, clr
  Register register_6 (.D(in_3), .Q(register_6_q), .clk(CLK));  // open: en, clr
  Register register_7 (.D(in_12), .Q(register_7_q));  // open: en, clk, clr
  Adder adder_3 (.a(register_6_q), .b(register_7_q), .out(adder_3_out), .cout(adder_3_cout));  // open: cin
  Subtractor subtractor_1 (
    .a(register_6_q), .b(register_7_q), .out(subtractor_1_out), .bout(subtractor_1_bout));  // open: bin
  Multiplier multiplier_1 (
    .a(register_6_q), .b(register_7_q), .out(multiplier_1_out), .cout(multiplier_1_cout));  // open: cin
  Divider divider_1 (.a(register_6_q), .b(register_7_q), .out(divider_1_out), .rem(divider_1_rem));  // open: upper
  Multiplier multiplier_2 (
    .a(register_6_q), .b(register_6_q), .out(multiplier_2_out), .cout(multiplier_2_cout));  // open: cin
  Multiplier multiplier_3 (.a(register_6_q), .b(register_6_q), .out(multiplier_3_out));  // open: cin, cout
  Comparator comparator_3 (
    .a(register_6_q), .b(register_7_q), .gt(comparator_3_gt[0]), .eq(comparator_3_gt[1]),
    .lt(comparator_3_gt[2]));
  xor xor_3 (xor_3_out, adder_3_cout, subtractor_1_bout);
  Multiplier multiplier_4 (.a(multiplier_3_out), .b(register_6_q), .out(multiplier_4_out));  // open: cin, cout
  // XOR_Gate xor_4 has open pins: in0=xor_3_out, in1=xor_5_out, out=open
  Comparator comparator_4 (.a({8{1'b0}}), .b(multiplier_1_cout), .gt(comparator_4_gt));  // open: eq, lt
  assign controlled_buffer_5_out = undriven_7 ? adder_3_out : 8'bz;  // Controlled_Buffer controlled_buffer_5
  assign controlled_buffer_5_out = undriven_6 ? subtractor_1_out : 8'bz;  // Controlled_Buffer controlled_buffer_6
  assign controlled_buffer_5_out = undriven_5 ? multiplier_1_out : 8'bz;  // Controlled_Buffer controlled_buffer_7
  assign controlled_buffer_5_out = undriven_4 ? divider_1_out : 8'bz;  // Controlled_Buffer controlled_buffer_8
  assign controlled_buffer_5_out = undriven_3 ? multiplier_2_out : 8'bz;  // Controlled_Buffer controlled_buffer_9
  assign controlled_buffer_5_out = undriven_2 ? multiplier_4_out : 8'bz;  // Controlled_Buffer controlled_buffer_10
  Register register_8 (.D({{5{1'b0}}, comparator_3_gt}), .clk(CLK));  // open: en, Q, clr
  ExactlyOne xor_5 (.out(xor_5_out), .in0(comparator_4_gt), .in1(comparator_5_gt), .in2(comparator_6_gt));
  Comparator comparator_5 (.a({8{1'b0}}), .b(divider_1_rem), .gt(comparator_5_gt));  // open: eq, lt
  Comparator comparator_6 (.a({8{1'b0}}), .b(multiplier_2_cout), .gt(comparator_6_gt));  // open: eq, lt
  Clock clock_1 (.out(CLK));
  assign controlled_buffer_11_out = in_2 ? controlled_buffer_13_out : 8'bz;  // Controlled_Buffer controlled_buffer_11
  assign controlled_buffer_11_out = not_3_out ? controlled_buffer_5_out : 8'bz;  // Controlled_Buffer controlled_buffer_12
  not not_3 (not_3_out, in_2);
  assign controlled_buffer_13_out = in_5 ? register_9_q : 8'bz;  // Controlled_Buffer controlled_buffer_13
  Register register_9 (.D(controlled_buffer_11_out), .en(in_4), .Q(register_9_q), .clk(CLK));  // open: clr
  assign controlled_buffer_13_out = in_7 ? register_10_q : 8'bz;  // Controlled_Buffer controlled_buffer_14
  Register register_10 (.D(controlled_buffer_11_out), .en(in_6), .Q(register_10_q), .clk(CLK));  // open: clr
  assign controlled_buffer_13_out = in_9 ? register_11_q : 8'bz;  // Controlled_Buffer controlled_buffer_15
  Register register_11 (.D(controlled_buffer_11_out), .en(in_8), .Q(register_11_q), .clk(CLK));  // open: clr
  assign controlled_buffer_13_out = in_11 ? register_12_q : 8'bz;  // Controlled_Buffer controlled_buffer_16
  Register register_12 (.D(controlled_buffer_11_out), .en(in_10), .Q(register_12_q), .clk(CLK));  // open: clr

  // Notes on the sheet:
  //   contents of OutsideMemory (hex, n*v repeats v):
  //   0 c 1 55 aa 6 aa 3 55 aa 55
  //   《- 这个不要了
endmodule
